# Fritzing sketch Bio Med ESP32 Fritzing (saved by Fritzing 0.9.3b)

parts:
  U1 = LuaNode32 / ESP32
  J2 = female pin header, 2 pins [form="♀ (female)"]
  J4 = female pin header, 2 pins [form="♀ (female)"]
  J5 = female pin header, 1 pin [form="♀ (female)"]
  J3 = female pin header, 6 pins [form="♀ (female)"]
  J1 = female pin header, 4 pins [form="♀ (female)"]
  J6 = female pin header, 2 pins [form="♀ (female)"]

nets:
  N1: U1.D25, J4.pin1
  N2: U1.D26, J4.pin2
  N3: U1.D2, J3.pin3
  N4: U1.D4, J3.pin4
  N5: U1.RX2, J2.pin2, J5.pin1
  N6: U1.RX0, J1.pin2
  N7: J1.pin1, J6.pin2
  N8: J1.pin4, J6.pin1

notes:
  Weight Machine
  Blood Pressure Sensor
  IR Temperature Sensor
  Temp. Button
  Weight Button
  Rx
  Tx
  Gnd
  +5V
  Tx-Out
  Vin
  GY-MCU90615
  Rst
  Sim
  Vcc
  RS232 to TTL
  NC
  D2
  D4
  RX2
  RX0
  SW1
  SW2
  D25
  D26
  J17

custom parts:
  LuaNode32 / ESP32: ESP32 based LuaNode32
