# Fritzing sketch NodeMCU MUX (saved by Fritzing 0.9.3b)

parts:
  Part1 = Analog Digital MUX Breakout
  U1 = NodeMCU V1.0
  J1 = female pin header, 2 pins [form="♀ (female)"]
  J2 = female pin header, 2 pins [form="♀ (female)"]
  J3 = female pin header, 2 pins [form="♀ (female)"]
  J4 = female pin header, 2 pins [form="♀ (female)"]
  J5 = female pin header, 2 pins [form="♀ (female)"]
  J6 = female pin header, 2 pins [form="♀ (female)"]
  J7 = female pin header, 2 pins [form="♀ (female)"]
  J8 = female pin header, 2 pins [form="♀ (female)"]
  J9 = female pin header, 2 pins [form="♀ (female)"]
  J10 = female pin header, 2 pins [form="♀ (female)"]
  J11 = female pin header, 2 pins [form="♀ (female)"]
  J12 = female pin header, 2 pins [form="♀ (female)"]
  J13 = female pin header, 2 pins [form="♀ (female)"]
  J14 = female pin header, 2 pins [form="♀ (female)"]
  J15 = female pin header, 2 pins [form="♀ (female)"]
  J16 = female pin header, 2 pins [form="♀ (female)"]
  J17 = female pin header, 2 pins [form="♀ (female)"]
  J18 = female pin header, 2 pins [form="♀ (female)"]
  J19 = female pin header, 2 pins [form="♀ (female)"]
  J20 = female pin header, 2 pins [form="♀ (female)"]
  J21 = female pin header, 2 pins [form="♀ (female)"]
  J22 = female pin header, 2 pins [form="♀ (female)"]  # not connected
  J23 = female pin header, 2 pins [form="♀ (female)"]  # not connected
  J24 = female pin header, 2 pins [form="♀ (female)"]  # not connected

nets:
  N1: Part1.C0, J2.pin1
  N2: Part1.C1, J3.pin1
  N3: Part1.C2, J4.pin1
  N4: Part1.C3, J1.pin1
  N5: Part1.C4, J7.pin1
  N6: Part1.C5, J6.pin1
  N7: Part1.C6, J8.pin1
  N8: Part1.C7, J5.pin1
  N9: Part1.C8, J13.pin1
  N10: Part1.C9, J9.pin1
  N11: Part1.C10, J15.pin1
  N12: Part1.C11, J12.pin1
  N13: Part1.C12, J11.pin1
  N14: Part1.C13, J14.pin1
  N15: Part1.C14, J10.pin1
  N16: Part1.C15, J16.pin1
  GND: Part1.GND, Part1.EN, U1.GND, J18.pin1
  VCC: Part1.VCC, U1.D4, U1.3V3, J20.pin1
  N17: Part1.S0, U1.D5
  N18: Part1.S1, U1.D6
  N19: Part1.S2, U1.D7
  N20: Part1.S3, U1.D8
  N21: U1.D1, J17.pin1
  N22: U1.D2, J19.pin1
  N23: U1.D3, J21.pin1

custom parts:
  NodeMCU V1.0: ESP8266 based NodeMCU
